// Logisim project pipelined.circ as structural Verilog
module ALU_control (
  input  [1:0] ALUop,
  input  [5:0] Funct,
  input  [2:0] IMM_OP,
  output [3:0] Output
);

  // PLA #(.in_width(11), .out_width(4), .truth_table("00xxxxxxxxx,0010#lw/sw\n01xxxxxxxxx,0110#beq/bne\n10xxx100001,0010#addu\n10xxx100011,0110#subu\n10xxx100100,0000#AND\n10xxx100101,0001#OR\n10xxx100111,1100#nor\n10xxx101010,0111#slt\n11001xxxxxx,0010#addui\n11010xxxxxx,0111#slti\n11100xxxxxx,0000#andi\n11101xxxxxx,0001#ori\n10xxx000010,0010#jr\n10xxx000011,0010#jral")) pla_1: pin names not known; wires that end beside it: Output
endmodule

module Bit_extender (
  input  [15:0] Input,
  input  Signed,
  output [31:0] Output
);

  wire and_1_out;

  Multiplexer #(.width(16)) multiplexer_1 (.in0({16{1'b0}}), .in1({16{1'b1}}), .out(Output[31:16]), .sel(and_1_out));
  and and_1 (and_1_out, Input[15], Signed);

  assign Output[15:0] = Input;
endmodule

module main (
);

  wire and_1_out, clock_1_out, control_1_signedimm, EX_MEM_RegisterWriting_q, EX_MEM_Zero_q,
       MEM_WB_Branching_q, MEM_WB_Memory_q, mips_alu_1_p4, mipsprogramrom_1_p4, not_1_out, or_1_out,
       xor_1_out;
  wire [1:0] control_1_registerwriting, EX_MEM_Memory_q, forwarding_unit_1_forwarda,
       forwarding_unit_1_forwardb, ID_EX_RegisterWriting_q;
  wire [2:0] control_1_alu, control_1_memory, EX_MEM_Branching_q, ID_EX_Alu_q, ID_EX_Memory_q;
  wire [2:2] EX_MEM_Memory_q_2;
  wire [3:0] control_1_branching, ID_EX_Branching_q, ID_EX_PC_q_2, mips_alu_1_p3;
  wire [3:3] EX_MEM_Branching_q_2;
  wire [4:0] EX_MEM_RegDst_q, multiplexer_5_out, registerfile_1_p2;
  wire [23:0] EX_MEM_Result_q;
  wire [27:0] ID_EX_PC_q;
  wire [31:0] adder_1_out, adder_2_out, adder_3_out, bit_extender_1_output, EX_MEM_BranchPC_q,
       EX_MEM_JalPC_q, EX_MEM_JumpPC_q, ID_EX_IMM_q, ID_EX_OP_q, ID_EX_rd_q, ID_EX_rs_q, ID_EX_WriteData_q,
       IF_ID_OP_q, IF_ID_PC_q, MEM_WB_AluResult_q, MEM_WB_MemoryResult_q, mips_alu_1_p5, mips_ram_1_p6,
       mipsprogramrom_1_p2, multiplexer_1_out, multiplexer_2_out, multiplexer_3_out, multiplexer_4_out,
       multiplexer_6_out, multiplexer_7_out, PC_q, registerfile_1_p1, registerfile_1_p5, registerfile_1_p6,
       shifter_1_out;
  wire [31:24] EX_MEM_Result_q_2;

  Multiplexer #(.width(32)) multiplexer_1 (
    .in0(adder_1_out), .in1(multiplexer_6_out), .out(multiplexer_1_out), .sel(and_1_out));
  Adder #(.width(32)) adder_1 (.a(32'h4), .b(PC_q), .out(adder_1_out));  // open: cin, cout
  Register #(.width(32)) PC (.D(multiplexer_1_out), .en(1'b1), .Q(PC_q), .clk(clock_1_out));  // open: clr
  Clock clock_1 (.out(clock_1_out));
  // MIPSProgramROM mipsprogramrom_1: pin names not known; wires that end beside it: PC_q, mipsprogramrom_1_p2, clock_1_out, mipsprogramrom_1_p4
  Register #(.width(32)) IF_ID_PC (.D(adder_1_out), .en(1'b1), .Q(IF_ID_PC_q), .clk(clock_1_out));  // open: clr
  Register #(.width(32)) IF_ID_OP (
    .D(mipsprogramrom_1_p2), .en(1'b1), .Q(IF_ID_OP_q), .clk(clock_1_out), .clr(and_1_out));
  // RegisterFile #(.trigger("falling")) registerfile_1: pin names not known; wires that end beside it: registerfile_1_p1, registerfile_1_p2, IF_ID_OP_q[20:16], IF_ID_OP_q[25:21], registerfile_1_p5, registerfile_1_p6
  Bit_extender bit_extender_1 (.Input(IF_ID_OP_q[15:0]), .Signed(control_1_signedimm), .Output(bit_extender_1_output));
  Control control_1 (
    .Instruction(IF_ID_OP_q[31:26]), .Funct(IF_ID_OP_q[5:0]), .SignedIMM(control_1_signedimm),
    .Alu(control_1_alu), .Branching(control_1_branching), .Memory(control_1_memory),
    .RegisterWriting(control_1_registerwriting));
  Register #(.width(32)) ID_EX_PC (
    .D(IF_ID_PC_q), .en(1'b1), .Q({ID_EX_PC_q_2, ID_EX_PC_q}), .clk(clock_1_out));  // open: clr
  Register #(.width(32)) ID_EX_rd (.D(registerfile_1_p5), .en(1'b1), .Q(ID_EX_rd_q), .clk(clock_1_out));  // open: clr
  Register #(.width(32)) ID_EX_rs (.D(registerfile_1_p6), .en(1'b1), .Q(ID_EX_rs_q), .clk(clock_1_out));  // open: clr
  Register #(.width(32)) ID_EX_IMM (
    .D(bit_extender_1_output), .en(1'b1), .Q(ID_EX_IMM_q), .clk(clock_1_out));  // open: clr
  Register #(.width(3)) ID_EX_Alu (.D(control_1_alu), .en(1'b1), .Q(ID_EX_Alu_q), .clk(clock_1_out));  // open: clr
  Register #(.width(4)) ID_EX_Branching (
    .D(control_1_branching), .en(1'b1), .Q(ID_EX_Branching_q), .clk(clock_1_out), .clr(and_1_out));
  Register #(.width(32)) ID_EX_OP (.D(IF_ID_OP_q), .en(1'b1), .Q(ID_EX_OP_q), .clk(clock_1_out), .clr(and_1_out));
  Register #(.width(3)) ID_EX_Memory (
    .D(control_1_memory), .en(1'b1), .Q(ID_EX_Memory_q), .clk(clock_1_out), .clr(and_1_out));
  Register #(.width(2)) ID_EX_RegisterWriting (
    .D(control_1_registerwriting), .en(1'b1), .Q(ID_EX_RegisterWriting_q), .clk(clock_1_out), .clr(and_1_out));
  Shifter #(.width(32)) shifter_1 (.in(ID_EX_IMM_q), .\dist (5'b00010), .out(shifter_1_out));
  Multiplexer #(.width(32)) multiplexer_2 (
    .in0(ID_EX_IMM_q), .in1(ID_EX_rs_q), .out(multiplexer_2_out), .sel(ID_EX_Alu_q[0]));
  Multiplexer #(.select(2), .width(32)) multiplexer_3 (
    .in0(ID_EX_rd_q), .in1({EX_MEM_Result_q_2, EX_MEM_Result_q}), .in2(registerfile_1_p1),
    .out(multiplexer_3_out), .sel(forwarding_unit_1_forwarda));  // open: in3
  Multiplexer #(.select(2), .width(32)) multiplexer_4 (
    .in0(multiplexer_2_out), .in1({EX_MEM_Result_q_2, EX_MEM_Result_q}), .in2(registerfile_1_p1),
    .out(multiplexer_4_out), .sel(forwarding_unit_1_forwardb));  // open: in3
  Forwarding_unit forwarding_unit_1 (
    .EX_Mem_RegWrite(EX_MEM_RegisterWriting_q), .Mem_WB_RegWrite(mipsprogramrom_1_p4),
    .ForwardA(forwarding_unit_1_forwarda), .ForwardB(forwarding_unit_1_forwardb));  // open: ID_EX_RegisterRs, ID_EX_RegisterRt, EX_Mem_RegisterRd, EX_Mem_RegisterRt, Mem_WB_RegisterRd
  Adder #(.width(32)) adder_2 (.a(32'h4), .b({ID_EX_PC_q_2, ID_EX_PC_q}), .out(adder_2_out));  // open: cin, cout
  Adder #(.width(32)) adder_3 (
    .a({ID_EX_PC_q_2, ID_EX_PC_q}), .b(shifter_1_out), .out(adder_3_out));  // open: cin, cout
  // Mips_ALU mips_alu_1: pin names not known; wires that end beside it: multiplexer_3_out, multiplexer_4_out, mips_alu_1_p3, mips_alu_1_p4, mips_alu_1_p5
  ALU_control alu_control_1 (
    .ALUop(ID_EX_Alu_q[2:1]), .Output(mips_alu_1_p3), .Funct(ID_EX_OP_q[5:0]), .IMM_OP(ID_EX_OP_q[28:26]));
  Multiplexer #(.width(5)) multiplexer_5 (
    .in0(ID_EX_OP_q[20:16]), .in1(ID_EX_OP_q[15:11]), .out(multiplexer_5_out),
    .sel(ID_EX_RegisterWriting_q[0]));
  Register #(.width(32)) EX_MEM_JumpPC (
    .D({ID_EX_PC_q_2, ID_EX_OP_q[25:0], 2'b00}), .en(1'b1), .Q(EX_MEM_JumpPC_q), .clk(clock_1_out));  // open: clr
  Register #(.width(32)) EX_MEM_JalPC (.D(adder_2_out), .en(1'b1), .Q(EX_MEM_JalPC_q), .clk(clock_1_out));  // open: clr
  Register #(.width(32)) EX_MEM_BranchPC (
    .D(adder_3_out), .en(1'b1), .Q(EX_MEM_BranchPC_q), .clk(clock_1_out));  // open: clr
  Register #(.width(1)) EX_MEM_Zero (.D(mips_alu_1_p4), .en(1'b1), .Q(EX_MEM_Zero_q), .clk(clock_1_out));  // open: clr
  Register #(.width(32)) EX_MEM_Result (
    .D(mips_alu_1_p5), .en(1'b1), .Q({EX_MEM_Result_q_2, EX_MEM_Result_q}), .clk(clock_1_out));  // open: clr
  Register #(.width(32)) ID_EX_WriteData (
    .D(ID_EX_rs_q), .en(1'b1), .Q(ID_EX_WriteData_q), .clk(clock_1_out));  // open: clr
  Register #(.width(4)) EX_MEM_Branching (
    .D(ID_EX_Branching_q), .en(1'b1), .Q({EX_MEM_Branching_q_2[3], EX_MEM_Branching_q}), .clk(clock_1_out));  // open: clr
  Register #(.width(5)) EX_MEM_RegDst (
    .D(multiplexer_5_out), .en(1'b1), .Q(EX_MEM_RegDst_q), .clk(clock_1_out));  // open: clr
  Register #(.width(3)) EX_MEM_Memory (
    .D(ID_EX_Memory_q), .en(1'b1), .Q({EX_MEM_Memory_q_2[2], EX_MEM_Memory_q}), .clk(clock_1_out));  // open: clr
  Register #(.width(1)) EX_MEM_RegisterWriting (
    .D(ID_EX_RegisterWriting_q[1]), .en(1'b1), .Q(EX_MEM_RegisterWriting_q), .clk(clock_1_out));  // open: clr
  and and_1 (and_1_out, or_1_out, EX_MEM_Branching_q[0]);
  Multiplexer #(.select(2), .width(32)) multiplexer_6 (
    .in0(EX_MEM_JumpPC_q), .in1({EX_MEM_Result_q_2, EX_MEM_Result_q}), .in2(EX_MEM_BranchPC_q),
    .in3(EX_MEM_BranchPC_q), .out(multiplexer_6_out), .sel(EX_MEM_Branching_q[1:0]));
  or or_1 (or_1_out, EX_MEM_Branching_q[1], xor_1_out);
  xor xor_1 (xor_1_out, EX_MEM_Branching_q[2], EX_MEM_Zero_q);
  // MIPS_RAM #(.addrWidth(24)) mips_ram_1: pin names not known; wires that end beside it: EX_MEM_Result_q, ID_EX_WriteData_q, EX_MEM_Memory_q[1], EX_MEM_Memory_q[0], clock_1_out, mips_ram_1_p6
  Register #(.width(32)) MEM_WB_MemoryResult (
    .D(mips_ram_1_p6), .en(1'b1), .Q(MEM_WB_MemoryResult_q), .clk(clock_1_out));  // open: clr
  Register #(.width(32)) MEM_WB_AluResult (
    .D({EX_MEM_Result_q_2, EX_MEM_Result_q}), .en(1'b1), .Q(MEM_WB_AluResult_q), .clk(clock_1_out));  // open: clr
  Register #(.width(1)) MEM_WB_Branching (
    .D(EX_MEM_Branching_q_2[3]), .en(1'b1), .Q(MEM_WB_Branching_q), .clk(clock_1_out));  // open: clr
  Register #(.width(5)) MEM_WB_RegDst (
    .D(EX_MEM_RegDst_q), .en(1'b1), .Q(registerfile_1_p2), .clk(clock_1_out));  // open: clr
  Register #(.width(1)) MEM_WB_Memory (
    .D(EX_MEM_Memory_q_2[2]), .en(1'b1), .Q(MEM_WB_Memory_q), .clk(clock_1_out));  // open: clr
  Register #(.width(1)) MEM_WB_RegisterWriting (
    .D(EX_MEM_RegisterWriting_q), .en(1'b1), .Q(mipsprogramrom_1_p4), .clk(clock_1_out));  // open: clr
  Multiplexer #(.width(32)) multiplexer_7 (
    .in0(MEM_WB_AluResult_q), .in1(MEM_WB_MemoryResult_q), .out(multiplexer_7_out), .sel(MEM_WB_Memory_q));
  not not_1 (not_1_out, MEM_WB_Branching_q);
  Multiplexer #(.width(32)) multiplexer_8 (
    .in0(EX_MEM_JalPC_q), .in1(multiplexer_7_out), .out(registerfile_1_p1), .sel(not_1_out));

  // Notes on the sheet:
  //   contents of mipsprogramrom_1 (hex, n*v repeats v):
  //   addiu $1, $1, 0x1      # $1 = 0x0001     addiu $2, $2, 0x2      # $2 = 0x0002     slt $3, $1, $2
  //   # $3 = 1     slt $3, $2, $1         # $3 = 0     slti $3, $1, 0x1       # $3 = 1     slti $3, $1,
  //   0x42      # $3 = 0     or $3, $1, $2          # $3 = 0x3     and $3, $1, $2         # $3 = 0     ori
  //   $3, $1, 0x7        # $3 = 0x7     andi $3, $1, 0x7       # $3 = 0x1     sw $3, 0($0)     lw $5,
  //   0($0)     beq $1, $3, LOL
endmodule

module Control (
  input  [5:0] Instruction,
  input  [5:0] Funct,
  output SignedIMM,
  output [2:0] Alu,
  output [3:0] Branching,
  output [2:0] Memory,
  output [1:0] RegisterWriting
);

  PLA #(.in_width(6), .truth_table("001000,10#jr\n001001,11#jral")) jr_jral ();  // open: in, out
  PLA #(.in_width(8), .out_width(13), .truth_table("00000000,1100000001010#R-format\n000100xx,0000011000111#beq\n000101xx,0000011100111#bne\n001001xx,1000000001100#addiu\n001010xx,1000000001101#slti\n001100xx,1000000001100#andi\n001101xx,1000000001100#ori\n100011xx,1010100000001#lw\n101011xx,0001000000001#sw\n000010xx,0000010000000#j\n000011xx,0000010010000#jal\n00000010,0000010100000#jr\n00000011,0000010110000#jral")) pla_1 (.out(Branching));  // open: in
endmodule

module Forwarding_unit (
  input  EX_Mem_RegWrite,
  input  [7:0] ID_EX_RegisterRs,
  input  [7:0] ID_EX_RegisterRt,
  input  [7:0] EX_Mem_RegisterRd,
  input  [7:0] EX_Mem_RegisterRt,
  input  Mem_WB_RegWrite,
  input  [7:0] Mem_WB_RegisterRd,
  output [1:0] ForwardA,
  output [1:0] ForwardB
);

  wire and_1_out, and_2_out, comparator_1_eq, comparator_2_eq, comparator_3_eq, comparator_4_eq,
       comparator_5_eq, comparator_6_eq, comparator_7_eq, comparator_8_eq;

  Comparator #(.mode("unsigned")) comparator_1 (
    .a(ID_EX_RegisterRs), .b(EX_Mem_RegisterRd), .eq(comparator_1_eq));  // open: gt, lt
  Comparator #(.mode("unsigned")) comparator_2 (
    .a(EX_Mem_RegisterRd), .b({8{1'b0}}), .eq(comparator_2_eq));  // open: gt, lt
  Comparator #(.mode("unsigned")) comparator_3 (
    .a(EX_Mem_RegisterRd), .b({8{1'b0}}), .eq(comparator_3_eq));  // open: gt, lt
  Comparator #(.mode("unsigned")) comparator_4 (
    .a(ID_EX_RegisterRt), .b(EX_Mem_RegisterRt), .eq(comparator_4_eq));  // open: gt, lt
  Comparator #(.mode("unsigned")) comparator_5 (
    .a(Mem_WB_RegisterRd), .b({8{1'b0}}), .eq(comparator_5_eq));  // open: gt, lt
  Comparator #(.mode("unsigned")) comparator_6 (
    .a(ID_EX_RegisterRs), .b(Mem_WB_RegisterRd), .eq(comparator_6_eq));  // open: gt, lt
  Comparator #(.mode("unsigned")) comparator_7 (
    .a(Mem_WB_RegisterRd), .b(ID_EX_RegisterRt), .eq(comparator_7_eq));  // open: gt, lt
  Comparator #(.mode("unsigned")) comparator_8 (
    .a(EX_Mem_RegisterRd), .b(ID_EX_RegisterRt), .eq(comparator_8_eq));  // open: gt, lt
  and and_1 (and_1_out, EX_Mem_RegWrite, ~comparator_3_eq, ~comparator_6_eq);  // AND_Gate
  and and_2 (and_2_out, EX_Mem_RegWrite, ~comparator_3_eq, ~comparator_8_eq);  // AND_Gate
  and and_3 (ForwardA[1], EX_Mem_RegWrite, comparator_1_eq, ~comparator_2_eq);  // AND_Gate
  and and_4 (ForwardB[0], EX_Mem_RegWrite, comparator_3_eq, ~comparator_4_eq);  // AND_Gate
  and and_5 (ForwardA[0], Mem_WB_RegWrite, ~comparator_5_eq, ~and_1_out, comparator_6_eq);  // AND_Gate
  and and_6 (ForwardB[1], Mem_WB_RegWrite, ~comparator_5_eq, ~and_2_out, comparator_7_eq);  // AND_Gate
endmodule
